// Logisim project control-logic.circ as structural Verilog: 1 circuit, main circuit control_logic
module control_logic (
  input  [31:0] Instruction,
  input  BrEq,
  input  BrLt,
  output PCSel,
  output RegWEn,
  output [2:0] ImmSel,
  output BrUn,
  output ASel,
  output BSel,
  output [3:0] ALUSel,
  output MemWEn,
  output [1:0] WBSel
);

  wire and_12_out, and_13_out, and_14_out, and_15_out, and_16_out, AU_type, B_type, bitselector_6_out,
       bitselector_7_out, bitselector_8_out, bitselector_9_out, bitselector_10_out, bitselector_11_out,
       bitselector_12_out, BSuccess, fc3eq5, funct3_0, funct3_1, funct3_2, funct7_0, funct7_5, I_type,
       J_type, JI_type, L_type, LU_type, not_1_out, not_2_out, not_3_out, not_4_out, not_5_out, not_6_out,
       not_7_out, not_8_out, not_9_out, not_10_out, not_11_out, not_12_out, not_13_out, not_14_out,
       not_15_out, not_16_out, not_17_out, not_18_out, not_19_out, not_20_out, not_21_out, not_22_out,
       not_23_out, not_24_out, not_25_out, not_26_out, not_27_out, not_28_out, not_29_out, not_30_out,
       not_31_out, not_32_out, not_33_out, or_7_out, R_type, S_type, xor_1_out, xor_2_out;
  wire [1:0] priority_encoder_2_out;
  wire [3:0] priority_encoder_1_out, R_ALUSel;
  wire [3:3] I_ALUSel;

  BitSelector #(.width(7)) bitselector_1 (.in(Instruction[31:25]), .out(funct7_0), .sel(3'b000));
  BitSelector #(.width(7)) bitselector_2 (.in(Instruction[31:25]), .out(funct7_5), .sel(3'b101));
  BitSelector #(.width(3)) bitselector_3 (.in(Instruction[14:12]), .out(funct3_0), .sel(2'b00));
  BitSelector #(.width(3)) bitselector_4 (.in(Instruction[14:12]), .out(funct3_1), .sel(2'b01));
  BitSelector #(.width(3)) bitselector_5 (.in(Instruction[14:12]), .out(funct3_2), .sel(2'b10));
  or or_1 (MemWEn, L_type, S_type);
  Priority_Encoder #(.select_enc(4)) priority_encoder_1 (
    .in0(I_type), .in1(R_type), .in2(B_type), .in3(L_type), .in4(S_type), .in5(J_type), .in6(JI_type),
    .in7(AU_type), .in8(LU_type), .out(priority_encoder_1_out));  // open: in9, in10, in11, in12, in13, in14, in15
  // Probe on Instruction[6:0]
  or or_2 (PCSel, BSuccess, J_type, JI_type, AU_type);
  or or_3 (ASel, BSuccess, J_type, AU_type);
  or or_4 (RegWEn, I_type, R_type, L_type, J_type, JI_type, AU_type, LU_type);
  or or_5 (BSel, I_type, BSuccess, L_type, S_type, J_type, JI_type, AU_type, LU_type);
  // Probe on bitselector_6_out
  BitSelector #(.width(7)) bitselector_6 (.in(Instruction[6:0]), .out(bitselector_6_out), .sel(3'b000));
  // Probe on bitselector_7_out
  BitSelector #(.width(7)) bitselector_7 (.in(Instruction[6:0]), .out(bitselector_7_out), .sel(3'b001));
  // Probe on bitselector_8_out
  BitSelector #(.width(7)) bitselector_8 (.in(Instruction[6:0]), .out(bitselector_8_out), .sel(3'b010));
  // Probe on bitselector_9_out
  BitSelector #(.width(7)) bitselector_9 (.in(Instruction[6:0]), .out(bitselector_9_out), .sel(3'b011));
  // Probe on bitselector_10_out
  BitSelector #(.width(7)) bitselector_10 (.in(Instruction[6:0]), .out(bitselector_10_out), .sel(3'b100));
  // Probe on bitselector_11_out
  BitSelector #(.width(7)) bitselector_11 (.in(Instruction[6:0]), .out(bitselector_11_out), .sel(3'b101));
  // Probe on bitselector_12_out
  BitSelector #(.width(7)) bitselector_12 (.in(Instruction[6:0]), .out(bitselector_12_out), .sel(3'b110));
  Multiplexer #(.select(4), .width(3)) multiplexer_1 (
    .in0(3'b000), .in1(3'b000), .in2(3'b010), .in3(3'b000), .in4(3'b001), .in5(3'b100), .in6(3'b000),
    .in7(3'b011), .in8(3'b011), .out(ImmSel), .sel(priority_encoder_1_out));  // open: in9, in10, in11, in12, in13, in14, in15
  not not_1 (not_1_out, bitselector_8_out);
  not not_2 (not_2_out, bitselector_9_out);
  not not_3 (not_3_out, bitselector_11_out);
  not not_4 (not_4_out, bitselector_12_out);
  not not_5 (not_5_out, bitselector_8_out);
  not not_6 (not_6_out, bitselector_9_out);
  not not_7 (not_7_out, bitselector_12_out);
  not not_8 (not_8_out, bitselector_8_out);
  not not_9 (not_9_out, bitselector_9_out);
  not not_10 (not_10_out, bitselector_10_out);
  not not_11 (not_11_out, bitselector_8_out);
  not not_12 (not_12_out, bitselector_9_out);
  not not_13 (not_13_out, bitselector_10_out);
  not not_14 (not_14_out, bitselector_11_out);
  not not_15 (not_15_out, bitselector_12_out);
  not not_16 (not_16_out, bitselector_8_out);
  not not_17 (not_17_out, bitselector_9_out);
  not not_18 (not_18_out, bitselector_10_out);
  not not_19 (not_19_out, bitselector_12_out);
  not not_20 (not_20_out, bitselector_10_out);
  not not_21 (not_21_out, bitselector_9_out);
  not not_22 (not_22_out, bitselector_10_out);
  not not_23 (not_23_out, bitselector_9_out);
  not not_24 (not_24_out, bitselector_11_out);
  not not_25 (not_25_out, bitselector_12_out);
  not not_26 (not_26_out, bitselector_9_out);
  not not_27 (not_27_out, bitselector_12_out);
  Multiplexer #(.select(4), .width(4)) multiplexer_2 (
    .in0({I_ALUSel[3], Instruction[14:12]}), .in1(R_ALUSel), .in2(4'b0000), .in3(4'b0000), .in4(4'b0000),
    .in5(4'b0000), .in6(4'b0000), .in7(4'b0000), .in8(4'b1111), .out(ALUSel), .sel(priority_encoder_1_out));  // open: in9, in10, in11, in12, in13, in14, in15
  and and_1 (I_type, bitselector_6_out, bitselector_7_out, not_1_out, not_2_out, bitselector_10_out, not_3_out, not_4_out);
  and and_2 (R_type, bitselector_6_out, bitselector_7_out, not_5_out, not_6_out, bitselector_10_out, bitselector_11_out, not_7_out);
  and and_3 (B_type, bitselector_6_out, bitselector_7_out, not_8_out, not_9_out, not_10_out, bitselector_11_out, bitselector_12_out);
  and and_4 (L_type, bitselector_6_out, bitselector_7_out, not_11_out, not_12_out, not_13_out, not_14_out, not_15_out);
  and and_5 (S_type, bitselector_6_out, bitselector_7_out, not_16_out, not_17_out, not_18_out, bitselector_11_out, not_19_out);
  and and_6 (J_type, bitselector_6_out, bitselector_7_out, bitselector_8_out, bitselector_9_out, not_20_out, bitselector_11_out, bitselector_12_out);
  and and_7 (JI_type, bitselector_6_out, bitselector_7_out, bitselector_8_out, not_21_out, not_22_out, bitselector_11_out, bitselector_12_out);
  and and_8 (AU_type, bitselector_6_out, bitselector_7_out, bitselector_8_out, not_23_out, bitselector_10_out, not_24_out, not_25_out);
  and and_9 (LU_type, bitselector_6_out, bitselector_7_out, bitselector_8_out, not_26_out, bitselector_10_out, bitselector_11_out, not_27_out);
  Multiplexer #(.select(4), .width(2)) multiplexer_3 (
    .in0(2'b01), .in1(2'b01), .in2(2'b00), .in3(2'b00), .in4(2'b00), .in5(2'b10), .in6(2'b10), .in7(2'b01),
    .in8(2'b01), .out(WBSel), .sel(priority_encoder_1_out));  // open: in9, in10, in11, in12, in13, in14, in15
  not not_28 (not_28_out, funct3_1);
  not not_29 (not_29_out, funct7_0);
  not not_30 (not_30_out, funct7_5);
  not not_31 (not_31_out, funct7_5);
  not not_32 (not_32_out, funct7_0);
  and and_10 (BrUn, funct3_1, B_type);
  and u_fc3eq5 (fc3eq5, funct3_0, not_28_out, funct3_2);
  and and_11 (I_ALUSel[3], fc3eq5, funct7_5);
  and and_12 (and_12_out, not_29_out, not_30_out);
  and and_13 (and_13_out, funct7_0, not_31_out);
  and and_14 (and_14_out, not_32_out, funct7_5);
  xor xor_1 (xor_1_out, funct3_0, BrEq);
  not not_33 (not_33_out, funct3_2);
  xor xor_2 (xor_2_out, funct3_0, BrLt);
  Priority_Encoder #(.select_enc(2)) priority_encoder_2 (
    .in0(and_12_out), .in2(and_13_out), .in3(and_14_out), .out(priority_encoder_2_out));  // open: in1, gs, en_out, en_in
  and and_15 (and_15_out, xor_1_out, not_33_out);
  and and_16 (and_16_out, xor_2_out, funct3_2);
  assign R_ALUSel = {1'b0, Instruction[14:12]} | {priority_encoder_2_out, 2'b00};  // OR_Gate or_6, 4 bits wide
  or or_7 (or_7_out, and_15_out, and_16_out);
  and and_17 (BSuccess, B_type, or_7_out);

  // Other names for the same wires on the sheet: funct3[2:0] = Instruction[14:12]; I_ALUSel[2:0] = Instruction[14:12]

  // Notes on the sheet:
  //   INPUTS to your circuit
  //   DON'T CHANGE THE LOCATIONS OF THE INPUTS AND OUTPUTS!
  //   OUTPUT from your circuit
endmodule
