// Logisim project partial-load.circ as structural Verilog: 1 circuit, main circuit partial_load
module partial_load (
  input  [31:0] Instruction,
  input  [31:0] MemAddress,
  input  [31:0] DataFromMem,
  output [31:0] DataToReg
);

  wire bitselector_1_out, bitselector_2_out;
  wire [31:0] LB_Data, LH_Data;

  Multiplexer #(.select(2), .width(8)) multiplexer_1 (
    .in0(DataFromMem[7:0]), .in1(DataFromMem[15:8]), .in2(DataFromMem[23:16]), .in3(DataFromMem[31:24]),
    .out(LB_Data[7:0]), .sel(MemAddress[1:0]));
  Multiplexer #(.select(2), .width(16)) multiplexer_2 (
    .in0(DataFromMem[15:0]), .in1(DataFromMem[23:8]), .in2(DataFromMem[31:16]), .out(LH_Data[15:0]),
    .sel(MemAddress[1:0]));  // open: in3
  Multiplexer #(.width(24)) multiplexer_3 (
    .in0({24{1'b0}}), .in1({24{1'b1}}), .out(LB_Data[31:8]), .sel(bitselector_1_out));
  BitSelector bitselector_1 (.in(LB_Data[7:0]), .out(bitselector_1_out), .sel(3'b111));
  Multiplexer #(.width(16)) multiplexer_4 (
    .in0({16{1'b0}}), .in1({16{1'b1}}), .out(LH_Data[31:16]), .sel(bitselector_2_out));
  BitSelector #(.width(16)) bitselector_2 (.in(LH_Data[15:0]), .out(bitselector_2_out), .sel(4'b1111));
  Multiplexer #(.select(3), .width(32)) multiplexer_5 (
    .in0(LB_Data), .in1(LH_Data), .in2(DataFromMem), .out(DataToReg), .sel(Instruction[14:12]));  // open: in3, in4, in5, in6, in7

  // Other names for the same wires on the sheet: Data_07_00[7:0] = DataFromMem[7:0];
  //   Data_15_00[15:0] = DataFromMem[15:0]; LW_Data[31:0] = DataFromMem; Data_15_08[7:0] = DataFromMem[15:8];
  //   Data_23_08[15:0] = DataFromMem[23:8]; Data_23_16[7:0] = DataFromMem[23:16];
  //   Data_31_16[15:0] = DataFromMem[31:16]; Data_31_24[7:0] = DataFromMem[31:24]; funct3[2:0] = Instruction[14:12];
  //   Bottom_2[1:0] = MemAddress[1:0]

  // Notes on the sheet:
  //   INPUTS to your circuit
  //   DON'T CHANGE THE LOCATIONS OF THE INPUTS AND OUTPUTS!
  //   OUTPUT from your circuit
endmodule
