// Logisim project regfile.circ as structural Verilog: 1 circuit, main circuit regfile
module regfile (
  input  [4:0] ReadIndex1,
  input  [4:0] ReadIndex2,
  input  [4:0] WriteIndex,
  input  [31:0] WriteData,
  input  RegWEn,
  input  clk,
  output [31:0] ra,
  output [31:0] sp,
  output [31:0] t0,
  output [31:0] t1,
  output [31:0] t2,
  output [31:0] s0,
  output [31:0] s1,
  output [31:0] a0,
  output [31:0] ReadData1,
  output [31:0] ReadData2
);

  wire WE_0, WE_1, WE_2, WE_3, WE_4, WE_5, WE_6, WE_7, WE_8, WE_9, WE_10, WE_11, WE_12, WE_13, WE_14, WE_15,
       WE_16, WE_17, WE_18, WE_19, WE_20, WE_21, WE_22, WE_23, WE_24, WE_25, WE_26, WE_27, WE_28, WE_29,
       WE_30, WE_31;
  wire [31:0] output_x0, output_x3, output_x4, output_x11, output_x12, output_x13, output_x14, output_x15,
       output_x16, output_x17, output_x18, output_x19, output_x20, output_x21, output_x22, output_x23,
       output_x24, output_x25, output_x26, output_x27, output_x28, output_x29, output_x30, output_x31;

  Register #(.width(32)) register_1 (.D({32{1'b0}}), .en(WE_0), .clk(clk), .Q(output_x0));  // open: clr
  Register #(.width(32)) register_2 (.D(WriteData), .en(WE_4), .clk(clk), .Q(output_x4));  // open: clr
  Register #(.width(32)) register_3 (.D(WriteData), .en(WE_8), .clk(clk), .Q(s0));  // open: clr
  Register #(.width(32)) register_4 (.D(WriteData), .en(WE_12), .clk(clk), .Q(output_x12));  // open: clr
  Register #(.width(32)) register_5 (.D(WriteData), .en(WE_16), .clk(clk), .Q(output_x16));  // open: clr
  Register #(.width(32)) register_6 (.D(WriteData), .en(WE_20), .clk(clk), .Q(output_x20));  // open: clr
  Register #(.width(32)) register_7 (.D(WriteData), .en(WE_24), .clk(clk), .Q(output_x24));  // open: clr
  Register #(.width(32)) register_8 (.D(WriteData), .en(WE_28), .clk(clk), .Q(output_x28));  // open: clr
  Register #(.width(32)) register_9 (.D(WriteData), .en(WE_1), .clk(clk), .Q(ra));  // open: clr
  Register #(.width(32)) register_10 (.D(WriteData), .en(WE_5), .clk(clk), .Q(t0));  // open: clr
  Register #(.width(32)) register_11 (.D(WriteData), .en(WE_9), .clk(clk), .Q(s1));  // open: clr
  Register #(.width(32)) register_12 (.D(WriteData), .en(WE_13), .clk(clk), .Q(output_x13));  // open: clr
  Register #(.width(32)) register_13 (.D(WriteData), .en(WE_17), .clk(clk), .Q(output_x17));  // open: clr
  Register #(.width(32)) register_14 (.D(WriteData), .en(WE_21), .clk(clk), .Q(output_x21));  // open: clr
  Register #(.width(32)) register_15 (.D(WriteData), .en(WE_25), .clk(clk), .Q(output_x25));  // open: clr
  Register #(.width(32)) register_16 (.D(WriteData), .en(WE_29), .clk(clk), .Q(output_x29));  // open: clr
  Register #(.width(32)) register_17 (.D(WriteData), .en(WE_2), .clk(clk), .Q(sp));  // open: clr
  Register #(.width(32)) register_18 (.D(WriteData), .en(WE_6), .clk(clk), .Q(t1));  // open: clr
  Register #(.width(32)) register_19 (.D(WriteData), .en(WE_10), .clk(clk), .Q(a0));  // open: clr
  Register #(.width(32)) register_20 (.D(WriteData), .en(WE_14), .clk(clk), .Q(output_x14));  // open: clr
  Register #(.width(32)) register_21 (.D(WriteData), .en(WE_18), .clk(clk), .Q(output_x18));  // open: clr
  Register #(.width(32)) register_22 (.D(WriteData), .en(WE_22), .clk(clk), .Q(output_x22));  // open: clr
  Register #(.width(32)) register_23 (.D(WriteData), .en(WE_26), .clk(clk), .Q(output_x26));  // open: clr
  Register #(.width(32)) register_24 (.D(WriteData), .en(WE_30), .clk(clk), .Q(output_x30));  // open: clr
  Register #(.width(32)) register_25 (.D(WriteData), .en(WE_3), .clk(clk), .Q(output_x3));  // open: clr
  Register #(.width(32)) register_26 (.D(WriteData), .en(WE_7), .clk(clk), .Q(t2));  // open: clr
  Register #(.width(32)) register_27 (.D(WriteData), .en(WE_11), .clk(clk), .Q(output_x11));  // open: clr
  Register #(.width(32)) register_28 (.D(WriteData), .en(WE_15), .clk(clk), .Q(output_x15));  // open: clr
  Register #(.width(32)) register_29 (.D(WriteData), .en(WE_19), .clk(clk), .Q(output_x19));  // open: clr
  Register #(.width(32)) register_30 (.D(WriteData), .en(WE_23), .clk(clk), .Q(output_x23));  // open: clr
  Register #(.width(32)) register_31 (.D(WriteData), .en(WE_27), .clk(clk), .Q(output_x27));  // open: clr
  Register #(.width(32)) register_32 (.D(WriteData), .en(WE_31), .clk(clk), .Q(output_x31));  // open: clr
  Demultiplexer #(.select(5)) demultiplexer_1 (
    .out0(WE_0), .out1(WE_1), .out2(WE_2), .out3(WE_3), .out4(WE_4), .out5(WE_5), .out6(WE_6), .out7(WE_7),
    .out8(WE_8), .out9(WE_9), .out10(WE_10), .out11(WE_11), .out12(WE_12), .out13(WE_13), .out14(WE_14),
    .out15(WE_15), .out16(WE_16), .out17(WE_17), .out18(WE_18), .out19(WE_19), .out20(WE_20), .out21(WE_21),
    .out22(WE_22), .out23(WE_23), .out24(WE_24), .out25(WE_25), .out26(WE_26), .out27(WE_27), .out28(WE_28),
    .out29(WE_29), .out30(WE_30), .out31(WE_31), .in(RegWEn), .sel(WriteIndex));
  Multiplexer #(.select(5), .width(32)) multiplexer_1 (
    .in0(output_x0), .in1(ra), .in2(sp), .in3(output_x3), .in4(output_x4), .in5(t0), .in6(t1), .in7(t2),
    .in8(s0), .in9(s1), .in10(a0), .in11(output_x11), .in12(output_x12), .in13(output_x13),
    .in14(output_x14), .in15(output_x15), .in16(output_x16), .in17(output_x17), .in18(output_x18),
    .in19(output_x19), .in20(output_x20), .in21(output_x21), .in22(output_x22), .in23(output_x23),
    .in24(output_x24), .in25(output_x25), .in26(output_x26), .in27(output_x27), .in28(output_x28),
    .in29(output_x29), .in30(output_x30), .in31(output_x31), .out(ReadData1), .sel(ReadIndex1));
  Multiplexer #(.select(5), .width(32)) multiplexer_2 (
    .in0(output_x0), .in1(ra), .in2(sp), .in3(output_x3), .in4(output_x4), .in5(t0), .in6(t1), .in7(t2),
    .in8(s0), .in9(s1), .in10(a0), .in11(output_x11), .in12(output_x12), .in13(output_x13),
    .in14(output_x14), .in15(output_x15), .in16(output_x16), .in17(output_x17), .in18(output_x18),
    .in19(output_x19), .in20(output_x20), .in21(output_x21), .in22(output_x22), .in23(output_x23),
    .in24(output_x24), .in25(output_x25), .in26(output_x26), .in27(output_x27), .in28(output_x28),
    .in29(output_x29), .in30(output_x30), .in31(output_x31), .out(ReadData2), .sel(ReadIndex2));

  // Other names for the same wires on the sheet: output_x1[31:0] = ra; output_x2[31:0] = sp; output_x5[31:0] = t0;
  //   output_x6[31:0] = t1; output_x7[31:0] = t2; output_x8[31:0] = s0; output_x9[31:0] = s1; output_x10[31:0] = a0

  // Notes on the sheet:
  //   INPUTS to your circuit
  //   DON'T CHANGE THE LOCATIONS OF THE INPUTS AND OUTPUTS!
  //   These are DEBUG/TEST outputs from your circuit.
  //   OUTPUTS from your circuit
endmodule
